# Fritzing sketch therack (saved by Fritzing 1.0.4)
circuit board: 2.99999cm x 11cm
breadboards: 2

parts:
  100K = Rotary Potentiometer (Small) [maximum_resistance=100kΩ knob_status=50% power=0.5W package=THT]
  100K_2 = Rotary Potentiometer (Small) [maximum_resistance=100kΩ knob_status=50% power=0.5W package=THT]
  100K_3 = Rotary Potentiometer (Small) [maximum_resistance=100kΩ knob_status=50% power=0.5W package=THT]
  100K_4 = Resistor [tolerance=±5% resistance=100k power=0.25W package=THT]
  1K = Resistor [tolerance=±5% resistance=1k power=0.25W package=THT]
  072 = TL072 [package="DIP (Dual Inline) [THT]"]
  072_PWR = TL072 [package="DIP (Dual Inline) [THT]"]
  072_A = TL072 [package="DIP (Dual Inline) [THT]"]
  072_B = TL072 [package="DIP (Dual Inline) [THT]"]  # not connected
  IN = PJ-301M [part_number=PJ-301M]
  104 = Ceramic Capacitor [capacitance=100nF voltage=16V package="200 mil [THT, multilayer]"]
  J3 = shrouded pin header, 16 pins [form="♂ (shrouded male)"]
  100K1 = Resistor [tolerance=±5% resistance=100k power=0.25W package=THT]
  5817 = Diode [package=diode-1n4148]
  100uF = Electrolytic Capacitor [capacitance=0.1mF voltage=35V package="100 mil [THT, electrolytic]"]
  IN1 = PJ-301M [part_number=PJ-301M]
  IN2 = PJ-301M [part_number=PJ-301M]
  IN3 = PJ-301M [part_number=PJ-301M]
  IN4 = PJ-301M [part_number=PJ-301M]
  IN5 = PJ-301M [part_number=PJ-301M]
  IN6 = PJ-301M [part_number=PJ-301M]
  out = PJ-301M [part_number=PJ-301M]
  S1 = Taiway 100-SP-X-T1 SPDT Miniature Toggle Switch [part_number=100-SP-X-T1-0-0-B1-M2 package=THT]
  10K = Resistor [tolerance=±5% resistance=1k power=0.25W package=THT]
  470K = Resistor [tolerance=±5% resistance=470k power=0.25W package=THT]
  470K_2 = Resistor [tolerance=±5% resistance=470k power=0.25W package=THT]
  10nF = Film/Foil Capacitor [capacitance=100nF voltage=35V package="5mm [THT, pp]"]
  100nF1 = Film/Foil Capacitor [capacitance=100nF voltage=35V package="5mm [THT, pp]"]
  1uF = Electrolytic Capacitor [capacitance=1µF voltage=35V package="100 mil [THT, electrolytic]"]
  10uF = Electrolytic Capacitor [capacitance=10µF voltage=35V package="100 mil [THT, electrolytic]"]
  4040B = CD4040E [package="DIP16 [THT]"]
  CD4046 = IC, DIP package, 16 pins [chip_label=CD4046BE]
  100nF = Film/Foil Capacitor [capacitance=100nF voltage=35V package="5mm [THT, pp]"]
  100nF_2 = Film/Foil Capacitor [capacitance=100nF voltage=35V package="5mm [THT, pp]"]
  100nF_3 = Film/Foil Capacitor [capacitance=100nF voltage=35V package="5mm [THT, pp]"]
  100nF_4 = Film/Foil Capacitor [capacitance=100nF voltage=35V package="5mm [THT, pp]"]
  100nF_5 = Film/Foil Capacitor [capacitance=100nF voltage=35V package="5mm [THT, pp]"]
  100nF_6 = Film/Foil Capacitor [capacitance=100nF voltage=35V package="5mm [THT, pp]"]
  103 = Ceramic Capacitor [capacitance=10nF voltage=16V package="200 mil [THT, multilayer]"]
  103_2 = Ceramic Capacitor [capacitance=10nF voltage=16V package="200 mil [THT, multilayer]"]

nets:
  N1: 100K.leg1, IN4.Pin_2
  N2: 100K.wiper, 100K_3.leg1
  N3: 100K.leg2, IN5.Pin_2
  N4: 100K_2.leg1, IN3.Pin_2
  N5: 100K_2.wiper, 100K_3.leg2
  N6: 100K_2.leg2, IN2.Pin_2
  N7: 100K_3.wiper, out.Pin_3
  N8: 100K_4.Pin_0, 1K.Pin_1, 072.connector2, 072_A.pin3
  9V: 100K_4.Pin_1, 072.connector7, 072_PWR.pin8, 104.0, J3.pin5, J3.pin6, J3.pin11, J3.pin12, 100uF.+, 4040B.Vdd, CD4046.pin16, 103.0, 103_2.0
  GND: 1K.Pin_0, 072.connector3, 072_PWR.pin4, IN.Pin_1, 104.1, J3.pin2, J3.pin3, J3.pin4, J3.pin13, J3.pin14, J3.pin15, 100K1.Pin_1, 100uF.-, IN1.Pin_1, IN2.Pin_1, IN3.Pin_1, IN4.Pin_1, IN5.Pin_1, IN6.Pin_1, out.Pin_1, 10K.Pin_0, 100nF1.-, 1uF.-, 10uF.-, 4040B.Vss, CD4046.pin5, CD4046.pin8, 103.1, 103_2.1
  N9: 072.connector0, 072_A.pin1, 5817.A
  N10: 072.connector1, 072_A.pin2, IN.Pin_3, 100K1.Pin_0
  N11: J3.pin1, J3.pin16
  N12: J3.pin7, J3.pin10
  N13: J3.pin8, J3.pin9
  N14: 5817.C, CD4046.pin14
  N15: IN1.Pin_3, 100nF.-
  N16: IN2.Pin_3, 100nF_2.-
  N17: IN3.Pin_3, 100nF_3.-
  N18: IN4.Pin_3, 100nF_5.-
  N19: IN5.Pin_3, 100nF_4.-
  N20: IN6.Pin_3, 100nF_6.-
  N21: S1.COM, 470K_2.Pin_0, 100nF1.+
  N22: S1.L1, 10uF.+
  N23: S1.L2, 1uF.+
  N24: 10K.Pin_1, CD4046.pin11
  N25: 470K.Pin_0, 470K_2.Pin_1, CD4046.pin9
  N26: 470K.Pin_1, CD4046.pin13
  N27: 10nF.-, CD4046.pin7
  N28: 10nF.+, CD4046.pin6
  N29: 4040B.Q13, 100nF_5.+
  N30: 4040B.Q14, 100nF_4.+
  N31: 4040B.Q6, 100nF_6.+
  N32: 4040B.Q5, CD4046.pin3
  N33: 4040B.Q7, 100nF_3.+
  N34: 4040B.Q4, 100nF_2.+
  N35: 4040B.Q1, 100nF.+
  N36: 4040B.Input_signal, CD4046.pin4
  N37: 4040B.Reset, 4040B.Q9

notes:
  the rack
  blueprint@poetaster . de 2025
  jlcjlcjlcjlc

custom parts:
  TL072: Dual Operational Amplifier
  TL072: Dual Operational Amplifier
  TL072: Dual Operational Amplifier
  TL072: Dual Operational Amplifier
  PJ-301M: Phone power jack.
  CD4040E: CD4020B, CD4024B, and CD4040B are ripple-carry binary counters. All counter stages are master-slave flip-flops. The state of a counter advances one count on the negative transition of each input pulse; a high level on the RESET line resets the counter to its all zeros state. Schmitt trigger action on the input-pulse line permits unlimited rise and fall times. All inputs and outputs are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
